// Digital circuit COND_CHECKER.dig as structural Verilog
module COND_CHECKER (
  input  Z,
  input  C,
  input  N,
  input  V,
  input  COND_VALUE,
  input  [1:0] COND_FLAG,
  output COND_CHECKEROUT
);

  wire multiplexer_1_out;

  Multiplexer #(.Selector_Bits(2)) multiplexer_1 (
    .sel(COND_FLAG), .in_0(Z), .in_1(C), .in_2(N), .in_3(V), .out(multiplexer_1_out));
  xnor xnor_1 (COND_CHECKEROUT, multiplexer_1_out, COND_VALUE);
endmodule
