// Digital circuit CONTROL_UNIT.dig as structural Verilog
module CONTROL_UNIT (
  input  [5:0] uSTEP,
  input  [5:0] OPCODE,
  input  EN,
  output MDR_LOAD,
  output DEC_CLK,
  output DEC_LOAD,
  output FLAGS_LOAD_SEL0,
  output FLAGS_LOAD_SEL1,
  output MEM_DATA_SEL0,
  output MEM_DATA_SEL1,
  output JUMP_SEL,
  output COND_VALUE,
  output COND_FLAG0,
  output COND_FLAG1,
  output uSTEP_LOAD0,
  output uSTEP_LOAD1,
  output uSTEP_LOAD2,
  output uSTEP_LOAD3,
  output uSTEP_LOAD4,
  output uSTEP_LOAD5,
  output uSTEP_LOAD_EN,
  output CLK_STOP,
  output USE_CARRY,
  output uSTEP_RESET,
  output FLAGS_LOAD,
  output ALU_OP0,
  output ALU_OP1,
  output ALU_OP2,
  output ALU_OP3,
  output MEM_WRITE,
  output MEM_READ,
  output MAR_SEL0,
  output MAR_SEL1,
  output MAR_LOAD,
  output IMM_LOAD,
  output IR_LOAD,
  output PC_SEL,
  output PC_EN,
  output WB_SEL2,
  output WB_SEL1,
  output B_RW,
  output A_RW
);

  wire [8:0] MICROCODE_ROM_d;

  ROM #(.bigEndian("true"), .AddrBits(12), .Bits(48)) MICROCODE_ROM (
    .A({OPCODE, uSTEP}), .sel(EN),
    .D({A_RW, B_RW, WB_SEL1, WB_SEL2, PC_EN, PC_SEL, IR_LOAD, IMM_LOAD, MAR_LOAD, MAR_SEL1, MAR_SEL0, MEM_READ, MEM_WRITE, ALU_OP3, ALU_OP2, ALU_OP1, ALU_OP0, FLAGS_LOAD, uSTEP_RESET, USE_CARRY, CLK_STOP, uSTEP_LOAD_EN, uSTEP_LOAD5, uSTEP_LOAD4, uSTEP_LOAD3, uSTEP_LOAD2, uSTEP_LOAD1, uSTEP_LOAD0, COND_FLAG1, COND_FLAG0, COND_VALUE, JUMP_SEL, MEM_DATA_SEL1, MEM_DATA_SEL0, FLAGS_LOAD_SEL1, FLAGS_LOAD_SEL0, DEC_LOAD, DEC_CLK, MDR_LOAD, MICROCODE_ROM_d}));

  // Notes on the sheet:
  //   contents of MICROCODE_ROM (hex, n*v repeats v):
  //   a0000000000,40000000,900020000000,61*0,a0000000000,c0000000,900020000000
  //   ,61*0,a0000000000,1c0000000,900020000000,61*0,a0000000000,140000000
  //   ,900020000000,61*0,a0000000000,50000000,900020000000,61*0,a0000000000
  //   ,d0000000,900020000000,61*0,a0000000000,780000000,1c0000000,900020000000
  //   ,60*0,a0000000000,5c0000000,4580000,900780000000,9001c0000000
  //   ,20000000,58*0,a0000000000,5c0000000,4720000,0,900280000000,500300000000
  //   ,4110000,900020000000,56*0,a0000000000,c0000000,46a0000,900080000000
  //   ,0,4110000,500000000000,20000000,56*0,a0000000000,c0000000,4540000
  //   ,900080000000,4100000,20000000,58*0,a0000000000,c0000000,45a0000
  //   ,500080000000,9000a0000000,20000000,58*0,a0000000000,c0000000
  //   ,4580000,500080000000,9000a0000000,20000000,58*0,a0000000000,e0000000
  //   ,62*0,a0000000000,460000000,62*0,a0000000000,20000000,62*0,a0000000000
  //   ,900460000000,62*0,a0000000000,9004e0000000,62*0,a0000000000,900560000000
  //   ,62*0,a0000000000,9007e0000000,62*0,a0000000000,900660000000,62*0
  //   ,a0000000000,9006e0000000,62*0,a0000000000,900760000000,62*0,a0000000000
  //   ,500080000000,900080000000,500000000000,5005a0000000,59*0,a0000000000
  //   ,900260000000,62*0,a0000000000,9002e0000000,62*0,a0000000000,5c0000000
  //   ,900200000000,4580000,9001a0000000,20000000,58*0,a0000000000,500580000000
  //   ,900780000000,900180000000,900000000000,900180000000,440000000
  //   ,4d20000,900780000000,900280000000,500380000000,900000000000,9001a0000000
  //   ,9003a0000000,50*0,a0000000000,500580000000,900780000000,900180000000
  //   ,900000000000,900180000000,900200000000,900180000000,900200000000
  //   ,900180000000,900200000000,900180000000,500400000000,900280000000,900280000000,900280000000
  //   ,500080000000,900080000000,500000000000,5c0000000,5720000,500300000000
  //   ,900105310000,500080000000,900080000000,500020000000,38*0,a0000000000
  //   ,5004e0000000,62*0,a0000000000,900780000000,500460000000,61*0
  //   ,a0000000000,460000000,62*0,a0000000000,90000000000,8000000000
  //   ,801020000000,60*0,a0000000000,90000000000,8000000000,820000000
  //   ,60*0,a0000000000,90000000000,a00020000000,61*0,a0000000000,90000000000
  //   ,600020000000,61*0,a0000000000,90000000000,8000000000,820004000
  //   ,60*0,a0000000000,e000000000,801000000000,61*0,a0000000000,e000000000
  //   ,820000000,61*0,a0000000000,500580000000,900780000000,900180000000
  //   ,900060000000,59*0,a0000000000,500080000000,900080000000,500060000000
  //   ,60*0,a0000000000,900100000000,c000000000,820004000,60*0,a0000000000
  //   ,c000000000,401000000000,9001a0000000,60*0,a0000000000,900100000000
  //   ,c000000000,820008000,60*0,a0000000000,c000000000,1040002000,9001a0000000
  //   ,60*0,a0000000000,90000000000,98000000000,1000000200,8000000000
  //   ,80000c000,20000000,57*0,a0000000000,90000000000,90000000800,a90000000000
  //   ,600000000000,c000000000,1000000200,e000000000,80000c000,400,40002000
  //   ,5020000,500080000000,900180000000,500080000000,4510000,20000000
  //   ,47*0,a0000000000,90000000000,90000000800,a00000000000,c000000000
  //   ,800004000,400,40002000,4b20000,900180000000,4410000,20000000
  //   ,52*0,a0000000000,90000000000,a00000000000,c05a0000000,60*0,a0000000000
  //   ,90000000000,a00000000000,4500000,c0580000000,20000000,58*0,a0000000000
  //   ,90000000000,a00000000000,4520000,c0580000000,20000000,58*0,a0000000000
  //   ,90000000000,a00000000000,4540000,c0580000000,20000000,58*0,a0000000000
  //   ,90000000000,a00000000000,4560000,c0580000000,20000000,58*0,a0000000000
  //   ,90000000000,a00000000000,4580000,c0580000000,20000000,58*0,a0000000000
  //   ,90000000000,a00000000000,45a0000,c0580000000,20000000,58*0,a0000000000
  //   ,90000000000,a00000000000,45c0000,c0580000000,20000000,58*0,a0000000000
  //   ,90000000000,900100000000,c000000000,700000000000,800004000,600000000000
  //   ,500080000000,900080000000,500000000000,c0580000000,500080000000
  //   ,900080000000,500020000000,50*0,a0000000000,c000000000,401000000000
  //   ,500080000000,900080000000,500000000000,c0580000000,500080000000
  //   ,900080000000,500000000000,9001a0000000,53*0,a0000000000,90000000000
  //   ,8000000000,801000000000,20000000,59*0,a0000000000,90000000000
  //   ,8000000000,800000000,20000000,59*0,a0000000000,90000000000,8000000000
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endmodule
