// Digital circuit DEC_COUNTER.dig as structural Verilog
module DEC_COUNTER (
  input  [15:0] IMM_OUT,
  input  DEC_LOAD,
  input  DEC_CLK,
  output [15:0] DEC_COUNTOUT
);

  CounterPreset #(.Bits(16)) DEC_COUNTER (
    .en(1'b1), .C(DEC_CLK), .dir(1'b1), .in(IMM_OUT), .ld(DEC_LOAD), .clr(1'b0), .out(DEC_COUNTOUT));  // open: ovf
endmodule
