// Digital circuit FLAGS.dig as structural Verilog
module FLAGS (
  input  FLAGS_LOAD,
  input  [15:0] ALU_OUT,
  input  [15:0] MEMORY_BUS,
  input  [15:0] DEC_COUNT_OUT,
  input  FLAGS_LOAD_SEL1,
  input  FLAGS_LOAD_SEL0,
  input  CARRY_OUT,
  input  [3:0] ALU_OP,
  input  [15:0] RB,
  input  [15:0] RA,
  input  CLK,
  output Z,
  output C,
  output N,
  output V
);

  wire and_1_out, and_2_out, and_3_out, and_4_out, and_6_out, multiplexer_2_out, nor_1_out, not_1_out,
       not_2_out, not_3_out, not_4_out, not_5_out, not_6_out, or_1_out, or_2_out;
  wire [3:0] and_5_out, multiplexer_3_out;
  wire [15:0] multiplexer_1_out;

  not not_1 (not_1_out, RA[15]);
  not not_2 (not_2_out, RB[15]);
  not not_3 (not_3_out, multiplexer_1_out[15]);
  not not_4 (not_4_out, RA[15]);
  not not_5 (not_5_out, RB[15]);
  not not_6 (not_6_out, multiplexer_1_out[15]);
  and and_1 (and_1_out, not_4_out, not_5_out, multiplexer_1_out[15]);
  and and_2 (and_2_out, RA[15], RB[15], not_6_out);
  and and_3 (and_3_out, not_1_out, RB[15], multiplexer_1_out[15]);
  and and_4 (and_4_out, RA[15], not_2_out, not_3_out);
  or or_1 (or_1_out, and_1_out, and_2_out);
  or or_2 (or_2_out, and_3_out, and_4_out);
  Multiplexer #(.Bits(16)) multiplexer_1 (
    .sel(FLAGS_LOAD_SEL1), .in_0(ALU_OUT), .in_1(DEC_COUNT_OUT), .out(multiplexer_1_out));
  Multiplexer multiplexer_2 (.sel(ALU_OP[0]), .in_0(or_1_out), .in_1(or_2_out), .out(multiplexer_2_out));
  and and_5 (and_5_out[3], multiplexer_2_out, nor_1_out);
  nor nor_1 (nor_1_out, ALU_OP[1], ALU_OP[2], ALU_OP[3]);
  nor nor_2 (and_5_out[0], multiplexer_1_out[0], multiplexer_1_out[1], multiplexer_1_out[2], multiplexer_1_out[3], multiplexer_1_out[4], multiplexer_1_out[5], multiplexer_1_out[6], multiplexer_1_out[7], multiplexer_1_out[8], multiplexer_1_out[9], multiplexer_1_out[10], multiplexer_1_out[11], multiplexer_1_out[12], multiplexer_1_out[13], multiplexer_1_out[14], multiplexer_1_out[15]);
  Multiplexer #(.Bits(4)) multiplexer_3 (
    .sel(FLAGS_LOAD_SEL0), .in_0({and_5_out[3], multiplexer_1_out[15], CARRY_OUT, and_5_out[0]}),
    .in_1(MEMORY_BUS[3:0]), .out(multiplexer_3_out));
  and and_6 (and_6_out, FLAGS_LOAD, CLK);
  Register #(.Bits(4)) FLAGS (.D(multiplexer_3_out), .C(and_6_out), .en(1'b1), .Q({V, N, C, Z}));
endmodule
