// Digital circuit IR_and_IMM.dig as structural Verilog
module IR_and_IMM (
  input  [15:0] PROG_ROM,
  input  CLK,
  input  IR_LOAD,
  input  IMM_LOAD,
  output [2:0] REG_B,
  output [2:0] REG_A,
  output [5:0] OPCODE,
  output [15:0] WB,
  output [15:0] MAR,
  output [15:0] DEC_COUNTER
);

  wire [3:0] IR_q;

  Register #(.Bits(16)) IR (.D(PROG_ROM), .C(CLK), .en(IR_LOAD), .Q({OPCODE, REG_A, REG_B, IR_q}));
  Register #(.Bits(16)) IMM (.D(PROG_ROM), .C(CLK), .en(IMM_LOAD), .Q(DEC_COUNTER));

  assign MAR = DEC_COUNTER;
  assign WB = DEC_COUNTER;
endmodule
