// Digital circuit MEMORY.dig as structural Verilog
module MEMORY (
  input  CPU_CLK,
  input  MEM_WRITE,
  input  MEM_READ,
  input  MAR_LOAD,
  input  MDR_LOAD,
  input  [15:0] IMM_OUT,
  input  [15:0] ALU_OUT,
  input  [15:0] RA,
  input  [15:0] RB,
  input  [1:0] MAR_SEL,
  input  Z,
  input  C,
  input  N,
  input  V,
  input  [1:0] MEM_DATA_SEL,
  output [15:0] MEM_OUT_BUS,
  output [15:0] port1,
  output [15:0] port2,
  output [15:0] port3,
  output [15:0] port4
);

  wire and_1_out, and_2_out, and_3_out, and_4_out, and_5_out, and_6_out, and_7_out, and_8_out, and_9_out,
       decoder_1_out_0, decoder_1_out_1, decoder_2_out_0, decoder_2_out_1, decoder_3_out_0, decoder_3_out_1,
       decoder_3_out_2, decoder_3_out_3;
  wire [13:0] MAR_q;
  wire [15:0] GPIO_PORT1_q, GPIO_PORT2_q, GPIO_PORT3_q, GPIO_PORT4_q, MDR_q, multiplexer_1_out,
       multiplexer_2_out, multiplexer_3_out;
  wire [15:14] MAR_q_2;

  Multiplexer #(.Selector_Bits(2), .Bits(16)) multiplexer_1 (
    .sel(MEM_DATA_SEL), .in_0(RA), .in_1(RB), .in_2({{12{1'b0}}, V, N, C, Z}), .in_3(MDR_q),
    .out(multiplexer_1_out));
  Multiplexer #(.Selector_Bits(2), .Bits(16)) multiplexer_2 (
    .sel(MAR_SEL), .in_0(IMM_OUT), .in_1(ALU_OUT), .in_2(RA), .in_3(RB), .out(multiplexer_2_out));
  Register #(.Bits(16)) MAR (.D(multiplexer_2_out), .C(CPU_CLK), .en(MAR_LOAD), .Q({MAR_q_2, MAR_q}));
  Register #(.Bits(16)) MDR (.D(MEM_OUT_BUS), .C(CPU_CLK), .en(MDR_LOAD), .Q(MDR_q));
  Decoder decoder_1 (.sel(MAR_q_2[15]), .out_0(decoder_1_out_0), .out_1(decoder_1_out_1));
  Decoder decoder_2 (.sel(MAR_q_2[14]), .out_0(decoder_2_out_0), .out_1(decoder_2_out_1));
  Decoder #(.Selector_Bits(2)) decoder_3 (
    .sel(MAR_q[1:0]), .out_0(decoder_3_out_0), .out_1(decoder_3_out_1), .out_2(decoder_3_out_2),
    .out_3(decoder_3_out_3));
  Multiplexer #(.Selector_Bits(2), .Bits(16)) multiplexer_3 (
    .sel(MAR_q[1:0]), .in_0(port4), .in_1(port3), .in_2(port2), .in_3(port1), .out(multiplexer_3_out));
  and and_1 (and_1_out, decoder_1_out_0, decoder_2_out_1);
  and and_2 (and_2_out, decoder_2_out_0, decoder_3_out_0, MEM_WRITE);
  and and_3 (and_3_out, decoder_2_out_0, decoder_3_out_1, MEM_WRITE);
  and and_4 (and_4_out, decoder_2_out_0, decoder_3_out_2, MEM_WRITE);
  and and_5 (and_5_out, decoder_2_out_0, decoder_3_out_3, MEM_WRITE);
  and and_6 (and_6_out, MEM_READ, decoder_2_out_0);
  Multiplexer #(.Bits(16)) multiplexer_4 (
    .sel(and_6_out), .in_0({16{1'b0}}), .in_1(multiplexer_3_out), .out(MEM_OUT_BUS));
  and and_7 (and_7_out, MEM_WRITE, decoder_1_out_1);
  and and_8 (and_8_out, MEM_READ, decoder_1_out_1);
  and and_9 (and_9_out, MEM_READ, and_1_out);
  RAMDualPort #(.AddrBits(15), .Bits(16)) RAM (
    .A({MAR_q_2[14], MAR_q}), .Din(multiplexer_1_out), .str(and_7_out), .C(CPU_CLK), .ld(and_8_out),
    .D(MEM_OUT_BUS));
  ROM #(.AddrBits(14), .Bits(16)) DATA_ROM (.A(MAR_q), .sel(and_9_out), .D(MEM_OUT_BUS));
  Register #(.Bits(16)) GPIO_PORT1 (.D(multiplexer_1_out), .C(CPU_CLK), .en(and_2_out), .Q(GPIO_PORT1_q));
  Register #(.Bits(16)) GPIO_PORT2 (.D(multiplexer_1_out), .C(CPU_CLK), .en(and_3_out), .Q(GPIO_PORT2_q));
  Register #(.Bits(16)) GPIO_PORT3 (.D(multiplexer_1_out), .C(CPU_CLK), .en(and_4_out), .Q(GPIO_PORT3_q));
  Register #(.Bits(16)) GPIO_PORT4 (.D(multiplexer_1_out), .C(CPU_CLK), .en(and_5_out), .Q(GPIO_PORT4_q));
  assign port1 = ~MEM_READ ? GPIO_PORT4_q : 16'bz;  // DriverInvSel driverinvsel_1
  assign port2 = ~MEM_READ ? GPIO_PORT3_q : 16'bz;  // DriverInvSel driverinvsel_2
  assign port3 = ~MEM_READ ? GPIO_PORT2_q : 16'bz;  // DriverInvSel driverinvsel_3
  assign port4 = ~MEM_READ ? GPIO_PORT1_q : 16'bz;  // DriverInvSel driverinvsel_4
endmodule
