// Digital circuit MICROSTEP_COUNTER.dig as structural Verilog
module MICROSTEP_COUNTER (
  input  CPU_CLK,
  input  uSTEP_RESET,
  input  uSTEP_LOAD_EN,
  input  [5:0] uSTEP_LOAD,
  input  JUMP_SEL,
  input  COND_CHECKER_OUT,
  output [5:0] uSTEP
);

  wire and_1_out, or_1_out;

  and and_1 (and_1_out, uSTEP_LOAD_EN, COND_CHECKER_OUT);
  or or_1 (or_1_out, JUMP_SEL, and_1_out);
  CounterPreset #(.Bits(6)) uSTEP_COUNTER (
    .en(1'b1), .C(CPU_CLK), .dir(1'b0), .in(uSTEP_LOAD), .ld(or_1_out), .clr(uSTEP_RESET), .out(uSTEP));  // open: ovf
endmodule
