// Digital circuit PROGRAM_COUNTER.dig as structural Verilog
module PROGRAM_COUNTER (
  input  CPU_CLK,
  input  PC_EN,
  input  [15:0] ALU_OUT,
  input  PC_SEL,
  output [15:0] PC_OUT
);

  CounterPreset #(.Bits(16), .isProgramCounter("true")) PC (
    .en(PC_EN), .C(CPU_CLK), .dir(1'b0), .in(ALU_OUT), .ld(PC_SEL), .clr(1'b0), .out(PC_OUT));  // open: ovf
endmodule
