// Digital circuit PROG_MEMORY.dig as structural Verilog
module PROG_MEMORY (
  input  [15:0] PC_OUT,
  output [15:0] PROG_ROM
);

  ROM #(.bigEndian("true"), .AddrBits(16), .Bits(16)) rom_1 (.A(PC_OUT), .sel(1'b1), .D(PROG_ROM));

  // Notes on the sheet:
  //   contents of rom_1 (hex, n*v repeats v):
  //   8870,a,8f00,b,0,ec70,1,ff70
endmodule
