// Digital circuit REG_BANK.dig as structural Verilog
module REG_BANK (
  input  [2:0] REG_A,
  input  CLK,
  input  [2:0] REG_B,
  input  A_RW,
  input  B_RW,
  input  [15:0] DATA_IN,
  output [15:0] RA,
  output [15:0] RB
);

  wire demultiplexer_1_out_0, demultiplexer_1_out_1, demultiplexer_1_out_2, demultiplexer_1_out_3,
       demultiplexer_1_out_4, demultiplexer_1_out_5, demultiplexer_1_out_6, demultiplexer_1_out_7,
       demultiplexer_2_out_0, demultiplexer_2_out_1, demultiplexer_2_out_2, demultiplexer_2_out_3,
       demultiplexer_2_out_4, demultiplexer_2_out_5, demultiplexer_2_out_6, demultiplexer_2_out_7;
  wire [15:0] A0_q, A1_q, A2_q, A3_q, A4_q, A5_q, A6_q, A7_q, B0_q, B1_q, B2_q, B3_q, B4_q, B5_q, B6_q, B7_q;

  Demultiplexer #(.Selector_Bits(3)) demultiplexer_1 (
    .sel(REG_A), .in(A_RW), .out_0(demultiplexer_1_out_0), .out_1(demultiplexer_1_out_1),
    .out_2(demultiplexer_1_out_2), .out_3(demultiplexer_1_out_3), .out_4(demultiplexer_1_out_4),
    .out_5(demultiplexer_1_out_5), .out_6(demultiplexer_1_out_6), .out_7(demultiplexer_1_out_7));
  Register #(.Bits(16)) A0 (.D(DATA_IN), .C(CLK), .en(demultiplexer_1_out_0), .Q(A0_q));
  Register #(.Bits(16)) A1 (.D(DATA_IN), .C(CLK), .en(demultiplexer_1_out_1), .Q(A1_q));
  Register #(.Bits(16)) A2 (.D(DATA_IN), .C(CLK), .en(demultiplexer_1_out_2), .Q(A2_q));
  Register #(.Bits(16)) A3 (.D(DATA_IN), .C(CLK), .en(demultiplexer_1_out_3), .Q(A3_q));
  Register #(.Bits(16)) A4 (.D(DATA_IN), .C(CLK), .en(demultiplexer_1_out_4), .Q(A4_q));
  Register #(.Bits(16)) A5 (.D(DATA_IN), .C(CLK), .en(demultiplexer_1_out_5), .Q(A5_q));
  Register #(.Bits(16)) A6 (.D(DATA_IN), .C(CLK), .en(demultiplexer_1_out_6), .Q(A6_q));
  Register #(.Bits(16)) A7 (.D(DATA_IN), .C(CLK), .en(demultiplexer_1_out_7), .Q(A7_q));
  Multiplexer #(.Bits(16), .Selector_Bits(3)) multiplexer_1 (
    .sel(REG_A), .in_0(A0_q), .in_1(A1_q), .in_2(A2_q), .in_3(A3_q), .in_4(A4_q), .in_5(A5_q), .in_6(A6_q),
    .in_7(A7_q), .out(RA));
  Demultiplexer #(.Selector_Bits(3)) demultiplexer_2 (
    .sel(REG_B), .in(B_RW), .out_0(demultiplexer_2_out_0), .out_1(demultiplexer_2_out_1),
    .out_2(demultiplexer_2_out_2), .out_3(demultiplexer_2_out_3), .out_4(demultiplexer_2_out_4),
    .out_5(demultiplexer_2_out_5), .out_6(demultiplexer_2_out_6), .out_7(demultiplexer_2_out_7));
  Register #(.Bits(16)) B0 (.D(DATA_IN), .C(CLK), .en(demultiplexer_2_out_0), .Q(B0_q));
  Register #(.Bits(16)) B1 (.D(DATA_IN), .C(CLK), .en(demultiplexer_2_out_1), .Q(B1_q));
  Register #(.Bits(16)) B2 (.D(DATA_IN), .C(CLK), .en(demultiplexer_2_out_2), .Q(B2_q));
  Register #(.Bits(16)) B3 (.D(DATA_IN), .C(CLK), .en(demultiplexer_2_out_3), .Q(B3_q));
  Register #(.Bits(16)) B4 (.D(DATA_IN), .C(CLK), .en(demultiplexer_2_out_4), .Q(B4_q));
  Register #(.Bits(16)) B5 (.D(DATA_IN), .C(CLK), .en(demultiplexer_2_out_5), .Q(B5_q));
  Register #(.Bits(16)) B6 (.D(DATA_IN), .C(CLK), .en(demultiplexer_2_out_6), .Q(B6_q));
  Register #(.Bits(16)) B7 (.D(DATA_IN), .C(CLK), .en(demultiplexer_2_out_7), .Q(B7_q));
  Multiplexer #(.Bits(16), .Selector_Bits(3)) multiplexer_2 (
    .sel(REG_B), .in_0(B0_q), .in_1(B1_q), .in_2(B2_q), .in_3(B3_q), .in_4(B4_q), .in_5(B5_q), .in_6(B6_q),
    .in_7(B7_q), .out(RB));
endmodule
