// Digital circuit SPECIAL_DIV.dig as structural Verilog
module SPECIAL_DIV (
  input  N,
  input  [5:0] OPCODE,
  input  uSTEP_RESET,
  input  [5:0] uSTEP,
  input  CLK,
  output DIV_CTRL,
  output [15:0] DIV_RESULT
);

  wire and_1_out, not_1_out, not_2_out, not_3_out, not_4_out, not_5_out, not_6_out, not_7_out, not_8_out,
       not_9_out;
  wire [0:0] and_2_out;
  wire [15:0] add_1_s, multiplexer_1_out;

  not not_1 (not_1_out, uSTEP[0]);
  not not_2 (not_2_out, uSTEP[1]);
  not not_3 (not_3_out, uSTEP[3]);
  not not_4 (not_4_out, uSTEP[4]);
  not not_5 (not_5_out, uSTEP[5]);
  not not_6 (not_6_out, OPCODE[1]);
  not not_7 (not_7_out, OPCODE[2]);
  not not_8 (not_8_out, OPCODE[4]);
  not not_9 (not_9_out, OPCODE[5]);
  and and_1 (and_1_out, OPCODE[0], not_6_out, not_7_out, OPCODE[3], not_8_out, not_9_out);
  and and_2 (and_2_out[0], not_1_out, not_2_out, uSTEP[2], not_3_out, not_4_out, not_5_out);
  and and_3 (DIV_CTRL, N, and_1_out);
  Register #(.Bits(16)) u_DIV_RESULT (.D(multiplexer_1_out), .C(CLK), .en(1'b1), .Q(DIV_RESULT));
  Add #(.Bits(16)) add_1 (.a({{15{1'b0}}, and_2_out[0]}), .b(DIV_RESULT), .c_i(1'b0), .s(add_1_s));  // open: c_o
  Multiplexer #(.Bits(16)) multiplexer_1 (
    .sel(uSTEP_RESET), .in_0(add_1_s), .in_1({16{1'b0}}), .out(multiplexer_1_out));
endmodule
