// Digital circuit SPECIAL_MUL.dig as structural Verilog
module SPECIAL_MUL (
  input  Z,
  input  [5:0] OPCODE,
  input  uSTEP_RESET,
  input  RA_BIT0,
  input  [15:0] RB,
  input  CLK,
  input  [5:0] uSTEP,
  output MUL_CTRL,
  output [15:0] MUL_RESULT
);

  wire and_1_out, and_2_out, and_3_out, and_4_out, not_1_out, not_2_out, not_3_out, not_4_out, not_5_out,
       not_6_out, not_7_out, not_8_out, not_9_out;
  wire [15:0] add_1_s, multiplexer_1_out, multiplexer_2_out;

  not not_1 (not_1_out, OPCODE[0]);
  not not_2 (not_2_out, OPCODE[1]);
  not not_3 (not_3_out, OPCODE[2]);
  not not_4 (not_4_out, OPCODE[4]);
  not not_5 (not_5_out, OPCODE[5]);
  not not_6 (not_6_out, uSTEP[2]);
  not not_7 (not_7_out, uSTEP[3]);
  not not_8 (not_8_out, uSTEP[4]);
  not not_9 (not_9_out, uSTEP[5]);
  and and_1 (and_1_out, not_1_out, not_2_out, not_3_out, OPCODE[3], not_4_out, not_5_out);
  and and_2 (and_2_out, uSTEP[0], uSTEP[1], not_6_out, not_7_out, not_8_out, not_9_out);
  and and_3 (and_3_out, Z, and_1_out);
  and and_4 (and_4_out, and_2_out, RA_BIT0);
  and and_5 (MUL_CTRL, and_3_out, uSTEP_RESET);
  Register #(.Bits(16)) u_MUL_RESULT (.D(multiplexer_2_out), .C(CLK), .en(1'b1), .Q(MUL_RESULT));
  Multiplexer #(.Bits(16)) multiplexer_1 (.sel(and_4_out), .in_0({16{1'b0}}), .in_1(RB), .out(multiplexer_1_out));
  Add #(.Bits(16)) add_1 (.a(multiplexer_1_out), .b(MUL_RESULT), .c_i(1'b0), .s(add_1_s));  // open: c_o
  Multiplexer #(.Bits(16)) multiplexer_2 (
    .sel(uSTEP_RESET), .in_0(add_1_s), .in_1({16{1'b0}}), .out(multiplexer_2_out));
endmodule
