// Digital circuit WB_SELECTOR.dig as structural Verilog
module WB_SELECTOR (
  input  [15:0] MEM_OUTBUS,
  input  [15:0] ALU_OUT,
  input  [15:0] DIV_RESULT,
  input  [15:0] MUL_RESULT,
  input  [15:0] IMM_OUT,
  input  [15:0] PC_OUT,
  input  DIV_CTRL,
  input  MUL_CTRL,
  input  [1:0] WB_SEL,
  output [15:0] DATA_IN
);

  wire [15:0] multiplexer_1_out, multiplexer_2_out;

  Multiplexer #(.Bits(16)) multiplexer_1 (.sel(DIV_CTRL), .in_0(ALU_OUT), .in_1(DIV_RESULT), .out(multiplexer_1_out));
  Multiplexer #(.Bits(16)) multiplexer_2 (
    .sel(MUL_CTRL), .in_0(multiplexer_1_out), .in_1(MUL_RESULT), .out(multiplexer_2_out));
  Multiplexer #(.Bits(16), .Selector_Bits(2)) multiplexer_3 (
    .sel(WB_SEL), .in_0(MEM_OUTBUS), .in_1(multiplexer_2_out), .in_2(IMM_OUT), .in_3(PC_OUT), .out(DATA_IN));
endmodule
