// Digital circuit FULL_PROCESSOR.dig as structural Verilog
module FULL_PROCESSOR (
  input  CPU_CLK,
  output [15:0] port3,
  output [15:0] port2,
  output [15:0] port1,
  output [15:0] port4
);

  wire alu_1_carry_out, cond_checker_1_cond_checkerout, control_unit_1_a_rw, control_unit_1_b_rw,
       control_unit_1_cond_value, control_unit_1_dec_clk, control_unit_1_dec_load, control_unit_1_flags_load,
       control_unit_1_flags_load_sel0, control_unit_1_flags_load_sel1, control_unit_1_imm_load,
       control_unit_1_ir_load, control_unit_1_jump_sel, control_unit_1_mar_load, control_unit_1_mdr_load,
       control_unit_1_mem_read, control_unit_1_mem_write, control_unit_1_pc_en, control_unit_1_pc_sel,
       control_unit_1_use_carry, control_unit_1_ustep_load_en, control_unit_1_ustep_reset, flags_1_c,
       flags_1_n, flags_1_v, flags_1_z, special_div_1_div_ctrl, special_mul_1_mul_ctrl;
  wire [1:0] control_unit_1_cond_flag1, control_unit_1_mar_sel1, control_unit_1_mem_data_sel1,
       control_unit_1_wb_sel2;
  wire [2:0] ir_and_imm_1_reg_a, ir_and_imm_1_reg_b;
  wire [3:0] control_unit_1_alu_op0;
  wire [5:0] control_unit_1_ustep_load2, ir_and_imm_1_opcode, microstep_counter_1_ustep;
  wire [15:0] alu_1_alu_out, dec_counter_1_dec_countout, ir_and_imm_1_dec_counter, ir_and_imm_1_mar,
       ir_and_imm_1_wb, memory_1_mem_out_bus, prog_memory_1_prog_rom, program_counter_1_pc_out,
       reg_bank_1_ra, reg_bank_1_rb, special_div_1_div_result, special_mul_1_mul_result,
       wb_selector_1_data_in;

  CONTROL_UNIT control_unit_1 (
    .uSTEP(microstep_counter_1_ustep), .OPCODE(ir_and_imm_1_opcode), .EN(1'b1),
    .MDR_LOAD(control_unit_1_mdr_load), .DEC_CLK(control_unit_1_dec_clk), .DEC_LOAD(control_unit_1_dec_load),
    .FLAGS_LOAD_SEL0(control_unit_1_flags_load_sel0), .FLAGS_LOAD_SEL1(control_unit_1_flags_load_sel1),
    .MEM_DATA_SEL0(control_unit_1_mem_data_sel1[0]), .MEM_DATA_SEL1(control_unit_1_mem_data_sel1[1]),
    .JUMP_SEL(control_unit_1_jump_sel), .COND_VALUE(control_unit_1_cond_value),
    .COND_FLAG0(control_unit_1_cond_flag1[0]), .COND_FLAG1(control_unit_1_cond_flag1[1]),
    .uSTEP_LOAD0(control_unit_1_ustep_load2[0]), .uSTEP_LOAD1(control_unit_1_ustep_load2[1]),
    .uSTEP_LOAD2(control_unit_1_ustep_load2[2]), .uSTEP_LOAD3(control_unit_1_ustep_load2[3]),
    .uSTEP_LOAD4(control_unit_1_ustep_load2[4]), .uSTEP_LOAD5(control_unit_1_ustep_load2[5]),
    .uSTEP_LOAD_EN(control_unit_1_ustep_load_en), .USE_CARRY(control_unit_1_use_carry),
    .uSTEP_RESET(control_unit_1_ustep_reset), .FLAGS_LOAD(control_unit_1_flags_load),
    .ALU_OP0(control_unit_1_alu_op0[0]), .ALU_OP1(control_unit_1_alu_op0[1]),
    .ALU_OP2(control_unit_1_alu_op0[2]), .ALU_OP3(control_unit_1_alu_op0[3]),
    .MEM_WRITE(control_unit_1_mem_write), .MEM_READ(control_unit_1_mem_read),
    .MAR_SEL0(control_unit_1_mar_sel1[1]), .MAR_SEL1(control_unit_1_mar_sel1[0]),
    .MAR_LOAD(control_unit_1_mar_load), .IMM_LOAD(control_unit_1_imm_load), .IR_LOAD(control_unit_1_ir_load),
    .PC_SEL(control_unit_1_pc_sel), .PC_EN(control_unit_1_pc_en), .WB_SEL2(control_unit_1_wb_sel2[0]),
    .WB_SEL1(control_unit_1_wb_sel2[1]), .B_RW(control_unit_1_b_rw), .A_RW(control_unit_1_a_rw));  // open: CLK_STOP
  MICROSTEP_COUNTER microstep_counter_1 (
    .CPU_CLK(CPU_CLK), .uSTEP_RESET(control_unit_1_ustep_reset),
    .uSTEP_LOAD_EN(control_unit_1_ustep_load_en), .uSTEP_LOAD(control_unit_1_ustep_load2),
    .JUMP_SEL(control_unit_1_jump_sel), .COND_CHECKER_OUT(cond_checker_1_cond_checkerout),
    .uSTEP(microstep_counter_1_ustep));
  SPECIAL_DIV special_div_1 (
    .N(flags_1_n), .OPCODE(ir_and_imm_1_opcode), .uSTEP_RESET(control_unit_1_ustep_reset),
    .uSTEP(microstep_counter_1_ustep), .CLK(CPU_CLK), .DIV_CTRL(special_div_1_div_ctrl),
    .DIV_RESULT(special_div_1_div_result));
  SPECIAL_MUL special_mul_1 (
    .Z(flags_1_z), .OPCODE(ir_and_imm_1_opcode), .uSTEP_RESET(control_unit_1_ustep_reset),
    .RA_BIT0(reg_bank_1_ra[0]), .RB(reg_bank_1_rb), .CLK(CPU_CLK), .uSTEP(microstep_counter_1_ustep),
    .MUL_CTRL(special_mul_1_mul_ctrl), .MUL_RESULT(special_mul_1_mul_result));
  WB_SELECTOR wb_selector_1 (
    .MEM_OUTBUS(memory_1_mem_out_bus), .ALU_OUT(alu_1_alu_out), .DIV_RESULT(special_div_1_div_result),
    .MUL_RESULT(special_mul_1_mul_result), .IMM_OUT(ir_and_imm_1_wb), .PC_OUT(program_counter_1_pc_out),
    .DIV_CTRL(special_div_1_div_ctrl), .MUL_CTRL(special_mul_1_mul_ctrl), .WB_SEL(control_unit_1_wb_sel2),
    .DATA_IN(wb_selector_1_data_in));
  ALU alu_1 (
    .USE_CARRY(control_unit_1_use_carry), .C_FLAG(flags_1_c), .RB(reg_bank_1_rb), .RA(reg_bank_1_ra),
    .A2(control_unit_1_alu_op0[2]), .A0(control_unit_1_alu_op0[0]), .A1(control_unit_1_alu_op0[1]),
    .A3(control_unit_1_alu_op0[3]), .ALU_OUT(alu_1_alu_out), .CARRY_OUT(alu_1_carry_out));
  DEC_COUNTER dec_counter_1 (
    .IMM_OUT(ir_and_imm_1_dec_counter), .DEC_LOAD(control_unit_1_dec_load), .DEC_CLK(control_unit_1_dec_clk),
    .DEC_COUNTOUT(dec_counter_1_dec_countout));
  PROGRAM_COUNTER program_counter_1 (
    .CPU_CLK(CPU_CLK), .PC_EN(control_unit_1_pc_en), .ALU_OUT(alu_1_alu_out), .PC_SEL(control_unit_1_pc_sel),
    .PC_OUT(program_counter_1_pc_out));
  REG_BANK reg_bank_1 (
    .REG_A(ir_and_imm_1_reg_a), .CLK(CPU_CLK), .REG_B(ir_and_imm_1_reg_b), .A_RW(control_unit_1_a_rw),
    .B_RW(control_unit_1_b_rw), .DATA_IN(wb_selector_1_data_in), .RA(reg_bank_1_ra), .RB(reg_bank_1_rb));
  IR_and_IMM ir_and_imm_1 (
    .PROG_ROM(prog_memory_1_prog_rom), .CLK(CPU_CLK), .IR_LOAD(control_unit_1_ir_load),
    .IMM_LOAD(control_unit_1_imm_load), .REG_B(ir_and_imm_1_reg_b), .REG_A(ir_and_imm_1_reg_a),
    .OPCODE(ir_and_imm_1_opcode), .WB(ir_and_imm_1_wb), .MAR(ir_and_imm_1_mar),
    .DEC_COUNTER(ir_and_imm_1_dec_counter));
  COND_CHECKER cond_checker_1 (
    .Z(flags_1_z), .C(flags_1_c), .N(flags_1_n), .V(flags_1_v), .COND_VALUE(control_unit_1_cond_value),
    .COND_FLAG(control_unit_1_cond_flag1), .COND_CHECKEROUT(cond_checker_1_cond_checkerout));
  PROG_MEMORY prog_memory_1 (.PC_OUT(program_counter_1_pc_out), .PROG_ROM(prog_memory_1_prog_rom));
  MEMORY memory_1 (
    .CPU_CLK(CPU_CLK), .MEM_WRITE(control_unit_1_mem_write), .MEM_READ(control_unit_1_mem_read),
    .MAR_LOAD(control_unit_1_mar_load), .MDR_LOAD(control_unit_1_mdr_load), .IMM_OUT(ir_and_imm_1_mar),
    .ALU_OUT(alu_1_alu_out), .RA(reg_bank_1_ra), .RB(reg_bank_1_rb), .MAR_SEL(control_unit_1_mar_sel1),
    .Z(flags_1_z), .C(flags_1_c), .N(flags_1_n), .V(flags_1_v), .MEM_DATA_SEL(control_unit_1_mem_data_sel1),
    .MEM_OUT_BUS(memory_1_mem_out_bus), .port1(port3), .port2(port2), .port3(port1), .port4(port4));
  FLAGS flags_1 (
    .FLAGS_LOAD(control_unit_1_flags_load), .ALU_OUT(alu_1_alu_out), .MEMORY_BUS(memory_1_mem_out_bus),
    .DEC_COUNT_OUT(dec_counter_1_dec_countout), .FLAGS_LOAD_SEL1(control_unit_1_flags_load_sel1),
    .FLAGS_LOAD_SEL0(control_unit_1_flags_load_sel0), .CARRY_OUT(alu_1_carry_out),
    .ALU_OP(control_unit_1_alu_op0), .RB(reg_bank_1_rb), .RA(reg_bank_1_ra), .CLK(CPU_CLK), .Z(flags_1_z),
    .C(flags_1_c), .N(flags_1_n), .V(flags_1_v));

  // Notes on the sheet:
  //   CPU_CLK: Hz: 50000
endmodule
