// Digital circuit ALU.dig as structural Verilog
module ALU (
  input  USE_CARRY,
  input  C_FLAG,
  input  [15:0] RB,
  input  [15:0] RA,
  input  A2,
  input  A0,
  input  A1,
  input  A3,
  output [15:0] ALU_OUT,
  output CARRY_OUT
);

  wire multiplexer_2_out;
  wire [15:0] add_1_s, and_1_out, multiplexer_1_out, multiplexer_4_out, multiplexer_5_out, or_1_out,
       xor_1_out, xor_2_out, xor_3_out;

  Multiplexer #(.Bits(16)) multiplexer_1 (.sel(A1), .in_0(RB), .in_1(16'h1), .out(multiplexer_1_out));
  assign xor_1_out = multiplexer_1_out ^ {16{A0}};  // XOr xor_1, 16 bits wide
  Multiplexer multiplexer_2 (.sel(USE_CARRY), .in_0(A0), .in_1(C_FLAG), .out(multiplexer_2_out));
  Add #(.Bits(16)) add_1 (.a(RA), .b(xor_1_out), .c_i(multiplexer_2_out), .s(add_1_s), .c_o(CARRY_OUT));
  Multiplexer #(.Selector_Bits(2), .Bits(16)) multiplexer_3 (
    .sel({A3, A2}), .in_0(add_1_s), .in_1(multiplexer_5_out), .in_2(xor_3_out), .in_3(xor_3_out),
    .out(ALU_OUT));
  assign xor_2_out = RB ^ RA;  // XOr xor_2, 16 bits wide
  Multiplexer #(.Selector_Bits(2), .Bits(16)) multiplexer_4 (
    .sel({A1, A0}), .in_0(and_1_out), .in_1(or_1_out), .in_2(xor_2_out), .in_3(RA), .out(multiplexer_4_out));
  assign xor_3_out = {16{A2}} ^ multiplexer_4_out;  // XOr xor_3, 16 bits wide
  assign or_1_out = RB | RA;  // Or or_1, 16 bits wide
  Multiplexer #(.Selector_Bits(2), .Bits(16)) multiplexer_5 (
    .sel({A1, A0}), .in_0({RA[14:0], 1'b0}), .in_1({1'b0, RA[15:1]}), .in_2({RB[14:0], 1'b0}),
    .in_3({1'b0, RB[15:1]}), .out(multiplexer_5_out));
  assign and_1_out = RB & RA;  // And and_1, 16 bits wide
endmodule
